# Fritzing sketch circuit (saved by Fritzing 0.9.3b)
breadboards: 1
perfboards: 1

parts:
  7_4V2 = Header 2 [package=molex-1x2_lock]
  Float_Switch1 = Header 2 [package=molex-1x2_lock]
  D4 = Rectifier Diode [part_number=1N4001 package="300 mil [THT]"]
  R17 = Resistor [tolerance=±5% resistance=10k package="1206 [SMD]"]
  R19 = Resistor [tolerance=±5% resistance=1k package="1206 [SMD]"]
  R20 = Resistor [tolerance=±5% resistance=1k package="1206 [SMD]"]
  R18 = Resistor [tolerance=±5% resistance=10k package="1206 [SMD]"]
  Soil_Moisture_Sensor = Header 2 [package=molex-1x2_lock]
  Mortor1 = Header 2 [package=molex-1x2_lock]
  U1 = attiny85 [package=dip]
  Part1 = FC-28 Soil Hygrometer Module
  U4 = TRANSISTOR_NPN_2 [package=to-92]
  Battery = Header 2 [package=molex-1x2_lock]
  Q1 = MOSFET-NCHANNEL [package=to220v]
  R21 = Trimmer Potentiometer [maximum_resistance=10kΩ package=THT]

nets:
  N1: 7_4V2.1, D4.cathode, Mortor1.1
  GND: 7_4V2.2, Float_Switch1.1, R17.Pin_1, R18.Pin_1, U1.Pin_4, U4.E, Battery.2, Q1.S, R21.leg2
  N2: Float_Switch1.2, U1.Pin_7
  N3: D4.anode, Mortor1.2, Q1.D
  N4: R17.Pin_0, R19.Pin_0, U1.Pin_2
  N5: R19.Pin_1, Q1.G
  N6: R20.Pin_0, R18.Pin_0, U1.Pin_5
  N7: R20.Pin_1, U4.B
  N8: Soil_Moisture_Sensor.1, Part1.NEG
  N9: Soil_Moisture_Sensor.2, Part1.POS
  N10: U1.Pin_3, R21.wiper
  N11: U1.Pin_6, Part1.DO
  3.3V: U1.Pin_8, Part1.VCC, Battery.1, R21.leg1
  N12: Part1.GND, U4.C

custom parts:
  FC-28 Soil Hygrometer Module: The FC-28 is a soil hygrometer module that uses the Texas Instruments LM393 comparator chip to provide an analog measurement of soil humidity. The digital output is high when soil moisture is over a certain threshold, as determined by adjusting the potentiometer.
  TRANSISTOR_NPN_2: Alternate TO-92 NPN BJT
